# Fritzing sketch thermostat sketch-pcb (saved by Fritzing 0.8.0b)
breadboards: 1

parts:
  Part1 = Arduino Uno (Rev3)
  Q1 = NPN-Transistor [package="TO92 [THT]"]
  Q2 = NPN-Transistor [package="TO92 [THT]"]
  Q3 = NPN-Transistor [package="TO92 [THT]"]
  S1 = Pushbutton [package="[THT]"]
  S2 = Pushbutton [package="[THT]"]
  S3 = Pushbutton [package="[THT]"]
  RHT1 = Humidity and Temperature Sensor RHT03
  U1 = XBee
  J2 = female pin header, 4 pins [form="♀ (female)"]
  J1 = screw terminal, 9 pins
  K3 = Relay [part_number=FRS1B-S package=THT]
  K1 = Relay [part_number=FRS1B-S package=THT]
  K2 = Relay [part_number=FRS1B-S package=THT]
  K4 = Relay [part_number=FRS1B-S package=THT]
  Q4 = NPN-Transistor [package="TO92 [THT]"]

nets:
  N1: Part1.A4/SDA, J2.pin2
  N2: Part1.A5/SCL, J2.pin1
  VCC: Part1.5V, Q1.C, Q2.C, Q3.C, RHT1.Vcc, U1.VCC, J2.pin4, Q4.C
  GND: Part1.GND, S1.Pin_3, S1.Pin_4, S2.Pin_3, S2.Pin_4, S3.Pin_3, S3.Pin_4, RHT1.GND_2, U1.GND, J2.pin3, K3.COIL1, K1.COIL1, K2.COIL2, K4.COIL1
  N3: Part1.D8, Q4.B
  N4: Part1.D9_PWM, S3.Pin_1, S3.Pin_2
  N5: Part1.D11_PWM/MOSI, RHT1.Data-signal
  N6: Part1.D0/RX, U1.pin3
  N7: Part1.D1/TX, U1.pin2
  N8: Part1.D3_PWM, S2.Pin_1, S2.Pin_2
  N9: Part1.D4, S1.Pin_1, S1.Pin_2
  N10: Part1.D5_PWM, Q3.B
  N11: Part1.D6_PWM, Q2.B
  N12: Part1.D7, Q1.B
  N13: Q1.E, K1.COIL2
  N14: Q2.E, K2.COIL1
  N15: Q3.E, K3.COIL2
  N16: J1.pin1, K4.A
  N17: J1.pin2, K4.B
  N18: J1.pin3, K3.A
  N19: J1.pin4, K3.B
  N20: J1.pin5, K2.B
  N21: J1.pin6, K2.A
  N22: J1.pin7, K1.A
  N23: J1.pin8, K1.B
  N24: J1.pin9, K3.C1, K3.C2, K1.C1, K1.C2, K2.C1, K2.C2, K4.C1, K4.C2
  N25: K4.COIL2, Q4.E

notes:
  www.geniusideastudio.com
  v062313-001
  GIS-LMI-LB-25-1
