# Fritzing sketch thermostat sketch (saved by Fritzing 0.8.0b)
breadboards: 1

parts:
  Part1 = Arduino Uno (Rev3)
  R1 = Resistor [tolerance=±5% resistance=220 package=THT]
  R2 = Resistor [tolerance=±5% resistance=220 package=THT]
  R3 = Resistor [tolerance=±5% resistance=220 package=THT]
  Q1 = NPN-Transistor [package="TO92 [THT]"]
  Q2 = NPN-Transistor [package="TO92 [THT]"]
  Q3 = NPN-Transistor [package="TO92 [THT]"]
  S1 = Pushbutton [package="[THT]"]
  S2 = Pushbutton [package="[THT]"]
  S3 = Pushbutton [package="[THT]"]
  LED1 = LED - 5mm [color="Red (633nm)" package="5 mm [THT]"]
  LED2 = LED - 5mm [color="Blue (430nm)" package="5 mm [THT]"]
  LED3 = LED - 5mm [color="Yellow (595nm)" package="5 mm [THT]"]
  RHT1 = Humidity and Temperature Sensor RHT03
  LCD1 = i2c LCD screen
  Part2 = Arduino Xbee Libellium Shield

nets:
  N1: Part1.A4/SDA, LCD1.SDA
  N2: Part1.A5/SCL, LCD1.SCL
  5V: Part1.5V, Q1.C, Q2.C, Q3.C, RHT1.Vcc, LCD1.VDD, Part2.+5V
  GND: Part1.GND, R1.Pin_0, R2.Pin_0, R3.Pin_0, S1.Pin_3, S1.Pin_4, S2.Pin_3, S2.Pin_4, S3.Pin_3, S3.Pin_4, RHT1.GND_2, LCD1.VSS, Part2.GND
  N3: Part1.D9_PWM, S3.Pin_1, S3.Pin_2
  N4: Part1.D11_PWM/MOSI, RHT1.Data-signal
  N5: Part1.D0/RX, Part2.M8RXD
  N6: Part1.D1/TX, Part2.M8TXD
  N7: Part1.D3_PWM, S2.Pin_1, S2.Pin_2
  N8: Part1.D4, S1.Pin_1, S1.Pin_2
  N9: Part1.D5_PWM, Q3.B
  N10: Part1.D6_PWM, Q2.B
  N11: Part1.D7, Q1.B
  N12: R1.Pin_1, LED1.cathode
  N13: R2.Pin_1, LED2.cathode
  N14: R3.Pin_1, LED3.cathode
  N15: Q1.E, LED1.anode
  N16: Q2.E, LED2.anode
  N17: Q3.E, LED3.anode

custom parts:
  i2c LCD screen: A standard character display, usually with 2x16 characters. Comes in many colors.
